# Fritzing sketch haycarrito (saved by Fritzing 0.7.1b)
breadboards: 2

parts:
  R1 = Resistor [tolerance=±5% resistance=51 package=THT]
  Atmega128 = Arduino Mega
  R2 = Resistor [tolerance=±5% resistance=330 package=THT]
  PA6 = LED - 3mm [color="Red (633nm)" package="3 mm [THT]"]
  PA7 = LED - 3mm [color="Yellow (592nm)" package="3 mm [THT]"]
  R3 = Resistor [tolerance=±5% resistance=330 package=THT]
  R4 = Resistor [tolerance=±5% resistance=330 package=THT]
  R5 = Resistor [tolerance=±5% resistance=82 package=THT]
  Transistor_2 = Voltage Regulator - Variable [part_number=LM317 package="TO220 [THT]"]
  R6 = Resistor [tolerance=±5% resistance=51 package=THT]
  R7 = Resistor [tolerance=±5% resistance=82 package=THT]
  J1 = male pin header, 4 pins [form="♂ (male)"]
  2N3904 = NPN-Transistor [part_number=2N3904 package="SOT-23 [SMD]"]
  Transistor = Voltage Regulator - 5V [part_number=LM317 package="DPak [SMD]"]
  R8 = Resistor [tolerance=±5% resistance=56 package=THT]
  R9 = Resistor [tolerance=±5% resistance=330 package=THT]
  2N3905 = NPN-Transistor [part_number=2N3904 package="SOT-23 [SMD]"]
  R10 = Resistor [tolerance=±5% resistance=56 package=THT]
  R11 = Resistor [tolerance=±5% resistance=330 package=THT]
  L293B = L293D [part_number=L293B package=THT]
  M1 = DC Motor
  M2 = DC Motor
  PA5 = LED - 3mm [color="Green (565nm)" package="3 mm [THT]"]

nets:
  N1: R1.Pin_0, J1.pin1, Transistor.GND
  N2: R1.Pin_1, R5.Pin_0, Transistor.input_voltage
  N3: Atmega128.D6, L293B.In_3
  N4: Atmega128.D5, L293B.In_4
  N5: Atmega128.D4, L293B.In_2
  N6: Atmega128.D3, L293B.In_1
  N7: Atmega128.+5V, R2.Pin_0, R3.Pin_0, R4.Pin_0, Transistor.output_voltage, R9.Pin_0, R11.Pin_0, L293B.Enable_1, L293B.+Vmotor, L293B.Enable_2, L293B.+V
  N8: Atmega128.GND, R5.Pin_1, R7.Pin_1, J1.pin4, 2N3904.2, 2N3905.2, L293B.0V
  N9: Atmega128.D18, Transistor_2.IN
  N10: Atmega128.D19, 2N3905.1, R11.Pin_1
  N11: Atmega128.D22, PA5.cathode
  N12: Atmega128.D24, PA6.cathode
  N13: Atmega128.D26, PA7.cathode
  N14: R2.Pin_1, PA5.anode
  N15: PA6.anode, R3.Pin_1
  N16: PA7.anode, R4.Pin_1
  N17: Transistor_2.ADJ, R6.Pin_1, R7.Pin_0
  N18: Transistor_2.OUT, R6.Pin_0, J1.pin2
  N19: J1.pin3, R8.Pin_1
  N20: 2N3904.0, R8.Pin_0
  N21: 2N3904.1, R9.Pin_1, R10.Pin_1
  N22: 2N3905.0, R10.Pin_0
  N23: L293B.Out_1_(_Controlled_by_Enable_1_), M1.pin_1
  N24: L293B.Out_2_(_Controlled_by_Enable_1_), M1.pin_2
  N25: L293B.Out_3_(_Controlled_by_Enable_2_), M2.pin_2
  N26: L293B.Out_4_(_Controlled_by_Enable_2_), M2.pin_1

notes:
  5V
  PD3 PD2
  PA5
  PA6
  PA7
  PB6 PB5 PE4 PE3
